# Fritzing sketch RGB Flashlight v3 (saved by Fritzing 0.8.7b)
circuit board: 12.7833cm x 9.21355cm
breadboards: 1

parts:
  R4 = Dial Potentiometer with switch
  R5 = Dial Potentiometer with switch
  R6 = Dial Potentiometer with switch
  TRINKET1 = Trinket 3V
  U1 = LIPO-2000mAh [package=lipo-2000]
  neopixel1 = Neopixel Ring 16
  S1 = SPST Switch [package=r_sw_th]
  S3 = Toggle Switch [package=THT]
  R7 = Resistor [tolerance=±5% resistance=10k package=THT]

nets:
  N1: R4.leg1, R5.leg1, R6.leg1, TRINKET1.no_name_yet#2, U1.-, neopixel1.GND, R7.Pin_1
  N2: R4.wiper, TRINKET1.no_name_yet#4
  N3: R4.leg2, R5.leg2, R6.leg2, TRINKET1.no_name_yet#6, S3.L1
  N4: R5.wiper, TRINKET1.no_name_yet#7
  N5: R6.wiper, TRINKET1.no_name_yet#3
  N6: TRINKET1.no_name_yet#1, neopixel1.VCC, S1.S
  N7: TRINKET1.no_name_yet#8, neopixel1.IN
  N8: TRINKET1.no_name_yet#9, S3.COM, R7.Pin_0
  N9: U1.+, S1.O

notes:
  Unregulated battery Power
  Regulated Power From Trinket

custom parts:
  Trinket 3V: Adafruit Trinket 3V
  Neopixel Ring 16: Neopixel Ring x16
